# Fritzing sketch noudini (saved by Fritzing 0.8.7b)
circuit board: 10.8581cm x 5.44291cm
breadboards: 1

parts:
  part = Arduino Uno (Rev3)
  LED = LED - 5mm [color="Red (633nm)" package="5 mm [THT]"]
  Resistor = Resistor [tolerance=±5% resistance=330 package=THT]
  Pushbutton = Pushbutton [package="[THT]"]
  Resistor_2 = Resistor [tolerance=±5% resistance=10k package=THT]

nets:
  N1: part.D13/SCK, Resistor.Pin_1
  N2: part.GND, LED.anode, Resistor_2.Pin_1
  N3: part.D7, Pushbutton.Pin_3, Pushbutton.Pin_4, Resistor_2.Pin_0
  N4: LED.cathode, Resistor.Pin_0
  N5: Pushbutton.Pin_1, Pushbutton.Pin_2
